# Fritzing sketch reset para RPi (saved by Fritzing 0.9.2b)

parts:
  Parte1 = Arduino Uno (Rev3)
  LED1 = LED - 5mm [color="Red (633nm)" package="5 mm [THT]"]
  S1 = Square Pushbutton
  IR1 = TSOP312.., 314.. [package=THT]
  Q1 = NPN-Transistor [package="TO92 [THT]"]
  CONN1 = USB connector [package=THT]
  R1 = Resistor [tolerance=±5% resistance=470 package=THT]
  R2 = Resistor [tolerance=±5% resistance=10k package=THT]
  X1 = USB Connectors [package=usb-a-s-silk-female]
  R3 = Resistor [tolerance=±5% resistance=1k package=THT]
  U1 = RELAY [package=relay-jzc]
  D1 = Rectifier Diode [part_number=1N4001 package="300 mil [THT]"]

nets:
  N1: Parte1.D8, R3.Pin_1
  N2: Parte1.D10_PWM/SS, IR1.Data
  N3: Parte1.D6_PWM, R1.Pin_1
  N4: Parte1.D7, S1.leg1, R2.Pin_0
  GND: Parte1.GND, LED1.cathode, S1.leg0, IR1.GND, CONN1.chassis6, X1.GND, U1.COIL2, D1.anode
  VIN: Parte1.VIN, IR1.Vs, Q1.E, CONN1.5V, R2.Pin_1, U1.MAIN
  N5: LED1.anode, R1.Pin_0
  N6: Q1.B, R3.Pin_0
  N7: Q1.C, U1.COIL1, D1.cathode
  N8: X1.VBUS, U1.NC

notes:
  Rele 5V
  1N4007
  1K
  470 ohm
  10 K
  Led
  BC547
  Pulsador N/O
  Tsop 31238
  Arduino UNO,mini Pro, Nano...
  Conector al alimentador de la Raspberry
  Conector a la Raspberry
